# Fritzing sketch Hardware Opstelling (saved by Fritzing 0.9.3b)
breadboards: 1

parts:
  Part1 = Arduino Nano (Rev3.0)
  RE1 = Rotary Encoder [package=THT]
  S1 = Pushbutton [package="[THT]"]
  LED4 = LED - 5mm [color="Red (633nm)" package="5 mm [THT]"]
  LED5 = LED - 5mm [color="Red (633nm)" package="5 mm [THT]"]
  LED6 = LED - 5mm [color="Red (633nm)" package="5 mm [THT]"]
  R1 = Resistor [tolerance=±5% resistance=330 package=THT]
  LED7 = LED - 5mm [color="Red (633nm)" package="5 mm [THT]"]
  LED8 = LED - 5mm [color="Green (570nm)" package="5 mm [THT]"]
  LCD1 = LCD screen
  hc-sr1 = hc-sr04
  R2 = Resistor [tolerance=±5% resistance=330 package=THT]
  R3 = Resistor [tolerance=±5% resistance=330 package=THT]
  J1 = Basic Servo
  LED9 = LED - 5mm [color="Red (633nm)" package="5 mm [THT]"]
  R4 = Resistor [tolerance=±5% resistance=10k package=THT]

nets:
  GND: Part1.GND, RE1.EncoderPinC, R1.Pin_0, LCD1.VSS, LCD1.R/W, LCD1.LED-, hc-sr1.GND, J1.gnd
  N1: Part1.D2, RE1.EncoderPinB
  N2: Part1.D3, hc-sr1.Echo
  N3: Part1.D4, RE1.EncoderPinA
  N4: Part1.D5, hc-sr1.Trig
  N5: Part1.D6, J1.pulse
  N6: Part1.D7, LCD1.DB7
  N7: Part1.D8, LCD1.DB6
  N8: Part1.D9, LCD1.DB5
  N9: Part1.D10, LCD1.DB4
  N10: Part1.D11/MOSI, LCD1.E
  N11: Part1.D12/MISO, LCD1.RS
  VCC: Part1.5V, S1.Pin_1, S1.Pin_2, LCD1.VDD, hc-sr1.VCC, R2.Pin_0, R3.Pin_0, J1.vcc
  N12: Part1.A5, LED8.anode
  N13: Part1.A4, LED7.anode
  N14: Part1.A3, LED6.anode
  N15: Part1.A2, LED5.anode
  N16: Part1.A1, LED4.anode
  N17: Part1.A0, LED9.anode
  N18: Part1.D13/SCK, S1.Pin_3, S1.Pin_4, R4.Pin_1
  N19: LED4.cathode, LED5.cathode, LED6.cathode, LED7.cathode, LED8.cathode, LED9.cathode, R4.Pin_0
  N20: LCD1.V0, R3.Pin_1
  N21: LCD1.LED+, R2.Pin_1
